// Logisim project 2.circ as structural Verilog: 1 circuit, main circuit comparison
module comparison (
  input  [1:0] inputa,
  input  [1:0] inputb,
  output areequal,
  output greaterthan,
  output lessthan
);
endmodule
