// Logisim project 4.circ as structural Verilog: 1 circuit, main circuit cla
module cla (
  input  [5:0] inputa,
  input  [5:0] inputb,
  input  carryin,
  output [5:0] carryout,
  output [5:0] generator,
  output [5:0] propagator
);
endmodule
