// Logisim project 5.circ as structural Verilog: 1 circuit, main circuit alu
module alu (
  input  [11:0] inputa,
  input  [11:0] inputb,
  input  [2:0] operation,
  output [11:0] aluout,
  output overflow,
  output carry,
  output zero
);
endmodule
