// Logisim project 1.circ as structural Verilog: 1 circuit, main circuit alu8
module alu8 (
  input  [11:0] a,
  input  [11:0] b,
  input  [3:0] op,
  input  sysclock,
  output [11:0] alur
);
endmodule
