// Logisim project 2.circ as structural Verilog: 1 circuit, main circuit instructions
module instructions (
  input  resetall,
  input  sysclock,
  input  jmp,
  input  [11:0] a,
  output [11:0] pc,
  output [3:0] op,
  output [2:0] rd,
  output [2:0] rs1,
  output [2:0] rs2,
  output [11:0] imm
);
endmodule
