// Logisim project 3.circ as structural Verilog: 1 circuit, main circuit regfile
module regfile (
  input  [2:0] rd,
  input  [11:0] alur,
  input  [11:0] pc,
  input  [11:0] imm,
  input  [3:0] op,
  input  wen,
  input  resetall,
  input  sysclock,
  output [11:0] x0,
  output [11:0] x1,
  output [11:0] x2,
  output [11:0] x3,
  output [11:0] x4,
  output [11:0] x5,
  output [11:0] x6,
  output [11:0] x7
);
endmodule
