// Logisim project 4.circ as structural Verilog: 1 circuit, main circuit cpu
module cpu (
  input  resetall,
  input  sysclock,
  output [11:0] pc,
  output [11:0] x0,
  output [11:0] x1,
  output [11:0] x2,
  output [11:0] x3,
  output [11:0] x4,
  output [11:0] x5,
  output [11:0] x6,
  output [11:0] x7
);
endmodule
