// Logisim project 2tester.circ as structural Verilog: 1 circuit, main circuit main
module main (
  output resetall,
  output sysclock,
  output jmp,
  output [11:0] pc,
  output [3:0] op,
  output [2:0] rd,
  output [2:0] rs1,
  output [2:0] rs2,
  output [11:0] imm,
  output halt
);

  wire catchfire;
  wire [8:0] counter_1_q;

  Clock clock_1 (.out(sysclock));
  Counter #(.width(9), .max('h1ff), .ongoal("stay")) counter_1 (
    .up(1'b1), .clk(sysclock), .carry(halt), .Q(counter_1_q));  // open: clr, load, count, D
  not not_1 (catchfire, halt);
  Comparator #(.width(9)) comparator_1 (.a(counter_1_q), .b(9'hff), .eq(resetall));  // open: gt, lt

  // Notes on the sheet:
  //   Place your subcircuit here.
endmodule
