// Logisim project 4tester.circ as structural Verilog: 1 circuit, main circuit main
module main (
  output resetall,
  output sysclock,
  output [11:0] pc,
  output [11:0] x0,
  output [11:0] x1,
  output [11:0] x2,
  output [11:0] x3,
  output [11:0] x4,
  output [11:0] x5,
  output [11:0] x6,
  output [11:0] x7,
  output halt
);

  wire catchfire;

  Clock clock_1 (.out(sysclock));
  Counter #(.ongoal("stay")) counter_1 (.up(1'b1), .clk(sysclock), .carry(halt));  // open: clr, load, count, D, Q
  not not_1 (catchfire, halt);

  assign resetall = 1'b0;

  // Notes on the sheet:
  //   Place your subcircuit here.
endmodule
